# Fritzing sketch Wiring (saved by Fritzing 0.9.1b)

parts:
  Part1 = Arduino Uno (Rev3)
  RHT1 = Humidity and Temperature Sensor RHT03
  U1 = Barometric Pressure Sensor
  U2 = mystery part, 3 pins [chip_label=?]

nets:
  N1: Part1.A4/SDA, U1.SCK
  N2: Part1.A5/SCL, U1.MOSI
  N3: Part1.D2, U2.pin1
  N4: Part1.D5_PWM, RHT1.Data-signal
  3V3: Part1.3V3, RHT1.Vcc
  N5: Part1.5V, U2.pin3
  N6: Part1.GND, RHT1.GND_1

notes:
  BMP085
  DHT22
  433Mhz OOK receiver
